# Fritzing sketch ArdSimX_Radio (saved by Fritzing 0.9.3b)
circuit board: 8.46667cm x 5.64444cm
breadboards: 2

parts:
  Part1 = Arduino Mega 2560 (Rev3)
  LED1 = LED - 5mm [color="White (4500K)" package="5 mm [THT]"]  # not connected
  R1 = Resistor [tolerance=±5% resistance=68 package=THT]  # not connected
  LED2 = LED - 5mm [color="White (4500K)" package="5 mm [THT]"]  # not connected
  LED3 = LED - 5mm [color="White (4500K)" package="5 mm [THT]"]
  R2 = Resistor [tolerance=±5% resistance=68 package=THT]  # not connected
  R3 = Resistor [tolerance=±5% resistance=68 package=THT]  # not connected
  LED4 = LED - 5mm [color="White (4500K)" package="5 mm [THT]"]  # not connected
  R4 = Resistor [tolerance=±5% resistance=6.8 package=THT]  # not connected
  S1 = Momentary Switch [package=ksa_sealed_tac_switch]
  S2 = Momentary Switch [package=ksa_sealed_tac_switch]
  S3 = Momentary Switch [package=ksa_sealed_tac_switch]
  S4 = Momentary Switch [package=ksa_sealed_tac_switch]
  R5 = Resistor [tolerance=±5% resistance=10k package="0402 [SMD]"]  # not connected
  R6 = Resistor [tolerance=±5% resistance=10k package="0402 [SMD]"]
  R7 = Resistor [tolerance=±5% resistance=10k package="0402 [SMD]"]
  R8 = Resistor [tolerance=±5% resistance=10k package="0402 [SMD]"]  # not connected
  LED5 = LED - 5mm [color="Red (660nm)" package="5 mm [THT]"]
  R9 = Resistor [tolerance=±5% resistance=150 package=THT]
  R10 = Resistor [tolerance=±5% resistance=10k package="0402 [SMD]"]
  R11 = Resistor [tolerance=±5% resistance=10k package="0402 [SMD]"]  # not connected
  R12 = Resistor [tolerance=±5% resistance=10k package="0402 [SMD]"]  # not connected
  R13 = Resistor [tolerance=±5% resistance=10k package="0402 [SMD]"]
  R14 = Resistor [tolerance=±5% resistance=10k package="0402 [SMD]"]
  RE1 = Hexadecimal Rotary Encoder [part_number=APEM-PT65-303 package=THT]
  R15 = Resistor [tolerance=±5% resistance=10k package="0402 [SMD]"]

nets:
  N1: Part1.GND, LED3.cathode, S1.3, S2.3, S3.3, S4.3, LED5.cathode
  N2: Part1.D13_PWM, S1.1
  N3: Part1.D11_PWM, S2.1, R6.Pin_1
  N4: Part1.D9_PWM, S3.1, R7.Pin_1
  N5: Part1.5V, R6.Pin_0, R7.Pin_0, R13.Pin_1, R14.Pin_1, R15.Pin_1
  N6: Part1.D7_PWM, S4.1
  N7: Part1.D53, R9.Pin_1
  N8: LED5.anode, R9.Pin_0
  N9: R10.Pin_0, RE1.Output4Pin
  N10: RE1.InputCommon, RE1.InputCommon2
