# Fritzing sketch radio_selectable (saved by Fritzing 0.9.3b)
circuit board: 8.46667cm x 5.64444cm
breadboards: 1

parts:
  Part1 = Arduino Mega 2560 (Rev3)
  LED1 = LED - 5mm [color="Green (555nm)" package="5 mm [THT]"]
  R1 = Resistor [tolerance=±5% resistance=220 package=THT]
  LED3 = LED - 5mm [color="Green (555nm)" package="5 mm [THT]"]
  R4 = Resistor [tolerance=±5% resistance=220 package=THT]
  LED2 = LED - 5mm [color="Green (555nm)" package="5 mm [THT]"]
  R5 = Resistor [tolerance=±5% resistance=220 package=THT]
  LED4 = LED - 5mm [color="Green (555nm)" package="5 mm [THT]"]
  LED5 = LED - 5mm [color="Green (555nm)" package="5 mm [THT]"]
  LED6 = LED - 5mm [color="Green (555nm)" package="5 mm [THT]"]
  R6 = Resistor [tolerance=±5% resistance=220 package=THT]
  R7 = Resistor [tolerance=±5% resistance=220 package=THT]
  R8 = Resistor [tolerance=±5% resistance=220 package=THT]
  Power_plug1 = Power plug  # not connected
  8x8_LED_Modul_mit_MAX1 = 8x8 LED Modul mit MAX7219 [package=THT]
  8x8_LED_Modul_mit_MAX2 = 8x8 LED Modul mit MAX7219 [package=THT]
  S1 = Momentary Switch [package=ksa_sealed_tac_switch]
  R9 = Resistor [tolerance=±5% resistance=220 package=THT]
  R10 = Resistor [tolerance=±5% resistance=220 package=THT]
  S2 = Momentary Switch [package=ksa_sealed_tac_switch]
  RE1 = Rotary Encoder [package=THT]
  RE2 = Rotary Encoder [package=THT]
  RE3 = Rotary Encoder [package=THT]
  RE4 = Rotary Encoder [package=THT]
  switch1 = Rotary_Switch_12x1

nets (from the breadboard view):
  N1: Part1.GND, LED1.cathode, LED2.anode, LED4.cathode, LED5.cathode, LED6.cathode, 8x8_LED_Modul_mit_MAX1.GND_Eingang, S1.4, S2.4, RE1.EncoderPinC, RE2.EncoderPinC, RE3.EncoderPinC, RE4.EncoderPinC
  N2: Part1.D13_PWM, LED1.anode, R1.Pin_0, R1.Pin_1
  N3: Part1.D12_PWM, R4.Pin_0, R4.Pin_1, LED2.cathode
  N4: Part1.D11_PWM, LED3.cathode, R5.Pin_0, R5.Pin_1
  N5: Part1.D10_PWM, LED6.anode, R6.Pin_0, R6.Pin_1
  N6: Part1.D9_PWM, LED5.anode, R7.Pin_0, R7.Pin_1
  N7: Part1.D8_PWM, LED4.anode, R8.Pin_0, R8.Pin_1
  N8: Part1.5V, R9.Pin_0, R10.Pin_0
  N9: Part1.D6_PWM, R10.Pin_1, S2.2
  N10: Part1.D7_PWM, S1.2, R9.Pin_1
  N11: Part1.D22, RE1.EncoderPinA
  N12: Part1.D23, RE1.EncoderPinB
  N13: Part1.D24, RE2.EncoderPinA
  N14: Part1.D25, RE2.EncoderPinB
  N15: Part1.D26, RE3.EncoderPinA
  N16: Part1.D27, RE3.EncoderPinB
  N17: Part1.D28, RE4.EncoderPinA
  N18: Part1.D29, RE4.EncoderPinB
  N19: Part1.D42, switch1.6
  N20: Part1.D44, switch1.7
  N21: Part1.D46, 8x8_LED_Modul_mit_MAX1.VCC_Eingang
  N22: Part1.D48, switch1.9
  N23: Part1.D50, switch1.10
  N24: Part1.D52, switch1.11
  N25: 8x8_LED_Modul_mit_MAX1.DOUT_Ausgang, 8x8_LED_Modul_mit_MAX2.DIN_Eingang
  N26: 8x8_LED_Modul_mit_MAX1.CS_Ausgang, 8x8_LED_Modul_mit_MAX2.CS_Eingang
  N27: 8x8_LED_Modul_mit_MAX1.CLK_Ausgang, 8x8_LED_Modul_mit_MAX2.CLK_Eingang
